# Fritzing sketch servo_pot (saved by Fritzing 0.9.3b)
breadboards: 1

parts:
  J1 = Basic Servo
  U1 = NodeMCU v3.0
  R1 = Rotary Potentiometer (Small) [maximum_resistance=100kΩ package=THT]

nets:
  GND: J1.gnd, U1.GND, R1.leg1
  VCC: J1.vcc, U1.3V3, R1.leg2
  N1: J1.pulse, U1.D1
  N2: U1.A0, R1.wiper

custom parts:
  NodeMCU v3.0: NodeMCU v3 Lua WIFI Development Board
